// Logisim project Project.circ as structural Verilog: 14 circuits, main circuit main
module main (
);

  wire [3:0] alu_1_out_4;
  wire [7:0] alu_1_out_3, undriven, undriven_2;

  register register_1 ();  // open: out_1, out_2
  ALU alu_1 (.out_3(alu_1_out_3), .in_1(undriven), .in_2(undriven_2), .out_4(alu_1_out_4));  // open: out_5

  // Notes on the sheet:
  //   PC
  //   ALU
endmodule

module Half_Adder (
  input  in_1,
  input  in_2,
  output out_3,
  output out_4
);

  wire not_1_out, or_1_out;

  or or_1 (or_1_out, in_1, in_2);
  and and_1 (out_4, in_1, in_2);
  and and_2 (out_3, or_1_out, not_1_out);
  not not_1 (not_1_out, out_4);
endmodule

module Full_Adder (
  input  in_1,
  input  in_2,
  input  in_3,
  output out_4,
  output out_5
);

  wire half_adder_1_out_3, half_adder_1_out_4, half_adder_2_out_4;

  Half_Adder half_adder_1 (.in_1(in_1), .in_2(in_2), .out_3(half_adder_1_out_3), .out_4(half_adder_1_out_4));
  Half_Adder half_adder_2 (.in_1(half_adder_1_out_3), .in_2(in_3), .out_3(out_4), .out_4(half_adder_2_out_4));
  or or_1 (out_5, half_adder_2_out_4, half_adder_1_out_4);
endmodule

module Addition (
  input  [7:0] ALU_Left,
  input  [7:0] ALU_Right,
  output [7:0] out_3,
  output Overflow
);

  wire full_adder_1_out_5, full_adder_2_out_5, full_adder_3_out_5, full_adder_4_out_5, full_adder_5_out_5,
       full_adder_6_out_5, half_adder_1_out_4;

  Half_Adder half_adder_1 (.in_1(ALU_Left[0]), .in_2(ALU_Right[0]), .out_3(out_3[0]), .out_4(half_adder_1_out_4));
  Full_Adder full_adder_1 (
    .in_1(half_adder_1_out_4), .in_2(ALU_Right[1]), .in_3(ALU_Left[1]), .out_4(out_3[1]),
    .out_5(full_adder_1_out_5));
  Full_Adder full_adder_2 (
    .in_1(full_adder_1_out_5), .in_2(ALU_Right[2]), .in_3(ALU_Left[2]), .out_4(out_3[2]),
    .out_5(full_adder_2_out_5));
  Full_Adder full_adder_3 (
    .in_1(full_adder_2_out_5), .in_2(ALU_Right[3]), .in_3(ALU_Left[3]), .out_4(out_3[3]),
    .out_5(full_adder_3_out_5));
  Full_Adder full_adder_4 (
    .in_1(full_adder_3_out_5), .in_2(ALU_Right[4]), .in_3(ALU_Left[4]), .out_4(out_3[4]),
    .out_5(full_adder_4_out_5));
  Full_Adder full_adder_5 (
    .in_1(full_adder_4_out_5), .in_2(ALU_Right[5]), .in_3(ALU_Left[5]), .out_4(out_3[5]),
    .out_5(full_adder_5_out_5));
  Full_Adder full_adder_6 (
    .in_1(full_adder_5_out_5), .in_2(ALU_Right[6]), .in_3(ALU_Left[6]), .out_4(out_3[6]),
    .out_5(full_adder_6_out_5));
  Full_Adder full_adder_7 (
    .in_1(full_adder_6_out_5), .in_2(ALU_Right[7]), .in_3(ALU_Left[7]), .out_4(out_3[7]), .out_5(Overflow));

  // Notes on the sheet:
  //   ALU-Out
endmodule

module _2_s_Complement (
  input  [7:0] in_1,
  output [7:0] out_2
);

  wire half_adder_1_out_4, half_adder_2_out_4, half_adder_3_out_4, half_adder_4_out_4, half_adder_5_out_4,
       half_adder_6_out_4, half_adder_7_out_4, not_1_out, not_2_out, not_3_out, not_4_out, not_5_out,
       not_6_out, not_7_out, not_8_out, not_9_out, or_1_out;

  not not_1 (not_1_out, in_1[6]);
  not not_2 (not_2_out, in_1[7]);
  not not_3 (not_3_out, in_1[3]);
  not not_4 (not_4_out, in_1[2]);
  not not_5 (not_5_out, in_1[4]);
  not not_6 (not_6_out, in_1[5]);
  not not_7 (not_7_out, not_9_out);
  not not_8 (not_8_out, in_1[1]);
  not not_9 (not_9_out, in_1[0]);
  or or_1 (or_1_out, not_7_out, not_9_out);
  Half_Adder half_adder_1 (.in_1(or_1_out), .in_2(not_9_out), .out_3(out_2[0]), .out_4(half_adder_1_out_4));
  Half_Adder half_adder_2 (.in_1(half_adder_1_out_4), .in_2(not_8_out), .out_3(out_2[1]), .out_4(half_adder_2_out_4));
  Half_Adder half_adder_3 (.in_1(half_adder_2_out_4), .in_2(not_4_out), .out_3(out_2[2]), .out_4(half_adder_3_out_4));
  Half_Adder half_adder_4 (.in_1(half_adder_3_out_4), .in_2(not_3_out), .out_3(out_2[3]), .out_4(half_adder_4_out_4));
  Half_Adder half_adder_5 (.in_1(half_adder_4_out_4), .in_2(not_5_out), .out_3(out_2[4]), .out_4(half_adder_5_out_4));
  Half_Adder half_adder_6 (.in_1(half_adder_5_out_4), .in_2(not_6_out), .out_3(out_2[5]), .out_4(half_adder_6_out_4));
  Half_Adder half_adder_7 (.in_1(half_adder_6_out_4), .in_2(not_1_out), .out_3(out_2[6]), .out_4(half_adder_7_out_4));
  Half_Adder half_adder_8 (.in_1(half_adder_7_out_4), .in_2(not_2_out), .out_3(out_2[7]));  // open: out_4
endmodule

module ALU (
  input  [7:0] in_1,
  input  [7:0] in_2,
  output [7:0] out_3,
  output [3:0] out_4,
  output out_5
);

  wire [7:0] multiplexer_1_out, n2_s_complement_1_out_2;

  _2_s_Complement u_2_s_complement_1 (.in_1(in_2), .out_2(n2_s_complement_1_out_2));
  Addition addition_1 (.out_3(out_3), .ALU_Left(multiplexer_1_out), .ALU_Right(in_1), .Overflow(out_4[0]));
  Multiplexer #(.width(8)) multiplexer_1 (
    .in0(in_2), .in1(n2_s_complement_1_out_2), .out(multiplexer_1_out), .sel(out_5));  // open: en

  // Notes on the sheet:
  //   ALU-L
  //   ALU-R
  //   Subtraction Selector
  //   Will be made internal
  //   Status
  //   ALU-OUT
  //   Bit 0 - Overflow
endmodule

module register (
  output [7:0] out_1,
  output [7:0] out_2
);

  wire not_1_out, not_2_out, not_3_out, not_4_out, not_5_out, not_6_out, not_7_out, not_8_out;

  not not_1 (not_1_out, out_1[0]);
  not not_2 (not_2_out, out_1[1]);
  not not_3 (not_3_out, out_1[2]);
  not not_4 (not_4_out, out_1[3]);
  not not_5 (not_5_out, out_1[4]);
  not not_6 (not_6_out, out_1[5]);
  not not_7 (not_7_out, out_1[6]);
  not not_8 (not_8_out, out_1[7]);
  S_R_Flip_Flop s_r_ff_1 (.S(out_1[0]), .R(not_1_out), .Q(out_2[0]));  // open: clk, Qn, preset, reset, en
  S_R_Flip_Flop s_r_ff_2 (.S(out_1[1]), .R(not_2_out), .Q(out_2[1]));  // open: clk, Qn, preset, reset, en
  S_R_Flip_Flop s_r_ff_3 (.S(out_1[2]), .R(not_3_out), .Q(out_2[2]));  // open: clk, Qn, preset, reset, en
  S_R_Flip_Flop s_r_ff_4 (.S(out_1[3]), .R(not_4_out), .Q(out_2[3]));  // open: clk, Qn, preset, reset, en
  S_R_Flip_Flop s_r_ff_5 (.S(out_1[4]), .R(not_5_out), .Q(out_2[4]));  // open: clk, Qn, preset, reset, en
  S_R_Flip_Flop s_r_ff_6 (.S(out_1[5]), .R(not_6_out), .Q(out_2[5]));  // open: clk, Qn, preset, reset, en
  S_R_Flip_Flop s_r_ff_7 (.S(out_1[6]), .R(not_7_out), .Q(out_2[6]));  // open: clk, Qn, preset, reset, en
  S_R_Flip_Flop s_r_ff_8 (.S(out_1[7]), .R(not_8_out), .Q(out_2[7]));  // open: clk, Qn, preset, reset, en
endmodule

module CU (
  output [2:0] out_1
);
endmodule

module multiplication (
  input  [7:0] in_1,
  input  [7:0] in_2,
  input  in_3,
  input  in_4,
  input  in_5
);

  wire undriven, undriven_2, undriven_3, undriven_4, undriven_5, undriven_6, undriven_7, undriven_8;

  Clock clock_1 ();  // open: out
  booth_encoder booth_encoder_1 (.in_1(in_3), .in_2(in_4), .in_3(in_5));  // open: out_4, out_5
  partial_product partial_product_1 (
    .in_10(undriven_2), .in_12(undriven), .in_1(in_1[7]), .in_2(in_1[6]), .in_3(in_1[5]), .in_4(in_1[4]),
    .in_5(in_1[3]), .in_6(in_1[2]), .in_7(in_1[1]), .in_8(in_1[0]));  // open: in_9, in_11, out_13, out_14, out_15, out_16, out_17, out_18, out_19, out_20
  partial_product partial_product_2 (
    .in_10(undriven_4), .in_11(undriven_2), .in_12(undriven_3), .in_1(in_1[7]), .in_2(in_1[6]),
    .in_3(in_1[5]), .in_4(in_1[4]), .in_5(in_1[3]), .in_6(in_1[2]), .in_7(in_1[1]), .in_8(in_1[0]));  // open: in_9, out_13, out_14, out_15, out_16, out_17, out_18, out_19, out_20
  partial_product partial_product_3 (
    .in_10(undriven_6), .in_11(undriven_5), .in_12(undriven_4), .in_1(in_1[7]), .in_2(in_1[6]),
    .in_3(in_1[5]), .in_4(in_1[4]), .in_5(in_1[3]), .in_6(in_1[2]), .in_7(in_1[1]), .in_8(in_1[0]));  // open: in_9, out_13, out_14, out_15, out_16, out_17, out_18, out_19, out_20
  partial_product partial_product_4 (
    .in_10(undriven_8), .in_11(undriven_7), .in_12(undriven_6), .in_1(in_1[7]), .in_2(in_1[6]),
    .in_3(in_1[5]), .in_4(in_1[4]), .in_5(in_1[3]), .in_6(in_1[2]), .in_7(in_1[1]), .in_8(in_1[0]));  // open: in_9, out_13, out_14, out_15, out_16, out_17, out_18, out_19, out_20
endmodule

module partial_product2 (
  output [7:0] out_1,
  output out_2,
  output out_3,
  output out_4,
  output [8:0] out_5
);

  wire and_1_out, and_2_out, and_3_out, and_4_out, and_5_out, and_6_out, and_7_out, and_8_out, and_9_out,
       and_10_out, and_11_out, and_12_out, and_13_out, and_14_out, and_15_out, and_16_out, or_1_out,
       or_2_out, or_3_out, or_4_out, or_5_out, or_6_out, or_7_out;

  and and_1 (and_1_out, out_1[7], out_3);
  xor xor_1 (out_5[8], and_1_out, out_4);
  and and_2 (and_2_out, out_1[6], out_3);
  and and_3 (and_3_out, out_1[7], out_2);
  or or_1 (or_1_out, and_3_out, and_2_out);
  xor xor_2 (out_5[7], or_1_out, out_4);
  and and_4 (and_4_out, out_1[6], out_2);
  and and_5 (and_5_out, out_1[5], out_3);
  or or_2 (or_2_out, and_4_out, and_5_out);
  xor xor_3 (out_5[6], or_2_out, out_4);
  and and_6 (and_6_out, out_1[5], out_2);
  and and_7 (and_7_out, out_1[4], out_3);
  or or_3 (or_3_out, and_6_out, and_7_out);
  xor xor_4 (out_5[5], or_3_out, out_4);
  and and_8 (and_8_out, out_1[3], out_3);
  and and_9 (and_9_out, out_1[4], out_2);
  or or_4 (or_4_out, and_9_out, and_8_out);
  xor xor_5 (out_5[4], or_4_out, out_4);
  and and_10 (and_10_out, out_1[3], out_2);
  and and_11 (and_11_out, out_1[2], out_3);
  or or_5 (or_5_out, and_10_out, and_11_out);
  xor xor_6 (out_5[3], or_5_out, out_4);
  and and_12 (and_12_out, out_1[1], out_3);
  and and_13 (and_13_out, out_1[2], out_2);
  or or_6 (or_6_out, and_13_out, and_12_out);
  xor xor_7 (out_5[2], or_6_out, out_4);
  and and_14 (and_14_out, out_1[1], out_2);
  and and_15 (and_15_out, out_1[0], out_3);
  or or_7 (or_7_out, and_14_out, and_15_out);
  xor xor_8 (out_5[1], or_7_out, out_4);
  and and_16 (and_16_out, out_1[0], out_2);
  xor xor_9 (out_5[0], and_16_out, out_4);
endmodule

module booth_encoder2 (
  output [7:0] out_1,
  output [4:0] out_2,
  output [4:0] out_3,
  output [4:0] out_4
);

  wire xnor_1_out, xnor_2_out, xnor_3_out, xnor_4_out, xnor_5_out;

  xor xor_1 (out_2[0], 1'b0, out_1[0]);
  xnor xnor_1 (xnor_1_out, out_1[0], out_1[1]);
  xor xor_2 (out_2[1], out_1[1], out_1[2]);
  xnor xnor_2 (xnor_2_out, out_1[2], out_1[3]);
  xor xor_3 (out_2[2], out_1[3], out_1[4]);
  xnor xnor_3 (xnor_3_out, out_1[4], out_1[5]);
  xor xor_4 (out_2[3], out_1[5], out_1[6]);
  xnor xnor_4 (xnor_4_out, out_1[6], out_1[7]);
  xor xor_5 (out_2[4], out_1[7], 1'b0);
  xnor xnor_5 (xnor_5_out, 1'b0, 1'b0);
  nor nor_1 (out_3[0], out_2[0], xnor_1_out);
  nor nor_2 (out_3[1], out_2[1], xnor_2_out);
  nor nor_3 (out_3[2], out_2[2], xnor_3_out);
  nor nor_4 (out_3[3], out_2[3], xnor_4_out);
  nor nor_5 (out_3[4], out_2[4], xnor_5_out);

  assign out_4 = {1'b0, out_1[7], out_1[5], out_1[3], out_1[1]};
endmodule

module booth_encoder (
  input  in_1,
  input  in_2,
  input  in_3,
  output out_4,
  output out_5
);

  wire and_1_out, not_1_out, or_1_out;

  not not_1 (not_1_out, in_3);
  or or_1 (or_1_out, in_1, in_2);
  and and_1 (and_1_out, in_1, in_2);
  // Transmission_Gate transmission_1: pin names not known; wires that end beside it: or_1_out, not_1_out, in_3, out_5
  // Transmission_Gate transmission_2: pin names not known; wires that end beside it: and_1_out, not_1_out, out_5
  xor xor_1 (out_4, in_1, in_2);
endmodule

module booth_decoder (
  input  M,
  input  x2,
  input  uj_1,
  input  x1,
  input  uj,
  output ppij
);

  wire and_1_out, and_2_out, or_1_out;

  and and_1 (and_1_out, x2, uj_1);
  and and_2 (and_2_out, x1, uj);
  or or_1 (or_1_out, and_1_out, and_2_out);
  xor xor_1 (ppij, M, or_1_out);
endmodule

module partial_product (
  input  in_1,
  input  in_2,
  input  in_3,
  input  in_4,
  input  in_5,
  input  in_6,
  input  in_7,
  input  in_8,
  input  in_9,
  input  in_10,
  input  in_11,
  input  in_12,
  output out_13,
  output out_14,
  output out_15,
  output out_16,
  output out_17,
  output out_18,
  output out_19,
  output out_20
);

  wire booth_encoder_1_out_4, booth_encoder_1_out_5;

  booth_encoder booth_encoder_1 (
    .in_1(in_10), .in_2(in_11), .in_3(in_12), .out_4(booth_encoder_1_out_4), .out_5(booth_encoder_1_out_5));
  booth_decoder booth_decoder_1 (
    .M(in_10), .x2(booth_encoder_1_out_4), .uj_1(in_9), .x1(booth_encoder_1_out_5), .uj(in_1), .ppij(out_13));
  booth_decoder booth_decoder_2 (
    .M(in_10), .x2(booth_encoder_1_out_4), .uj_1(in_1), .x1(booth_encoder_1_out_5), .uj(in_2), .ppij(out_14));
  booth_decoder booth_decoder_3 (
    .M(in_10), .x2(booth_encoder_1_out_4), .uj_1(in_2), .x1(booth_encoder_1_out_5), .uj(in_3), .ppij(out_15));
  booth_decoder booth_decoder_4 (
    .x2(booth_encoder_1_out_4), .uj_1(in_3), .x1(booth_encoder_1_out_5), .uj(in_4), .ppij(out_16));  // open: M
  booth_decoder booth_decoder_5 (
    .M(in_10), .x2(booth_encoder_1_out_4), .uj_1(in_4), .x1(booth_encoder_1_out_5), .uj(in_5), .ppij(out_17));
  booth_decoder booth_decoder_6 (
    .M(in_10), .x2(booth_encoder_1_out_4), .uj_1(in_5), .x1(booth_encoder_1_out_5), .uj(in_6), .ppij(out_18));
  booth_decoder booth_decoder_7 (
    .M(in_10), .x2(booth_encoder_1_out_4), .uj_1(in_6), .x1(booth_encoder_1_out_5), .uj(in_7), .ppij(out_19));
  booth_decoder booth_decoder_8 (
    .M(in_10), .x2(booth_encoder_1_out_4), .uj_1(in_7), .x1(booth_encoder_1_out_5), .uj(in_8), .ppij(out_20));
  // also tied to GND on the sheet: in_9
endmodule
